// Logisim project 16bitCPUPipelining.circ as structural Verilog: 11 circuits, main circuit main
module main (
  output [15:0] out_1,
  output [2:0] out_2
);

  wire alu_1_ble, ALU_src, and_1_out, and_2_out, arguments_1_first, arguments_1_second, ble, calc, call,
       call_mem, clk, clock_1_out, ex_mem_1_aluble_2, ex_mem_1_ble_2, ex_mem_1_calc_2, ex_mem_1_jtype_2,
       ex_mem_1_li_2, ex_mem_1_memread_2, ex_mem_1_memtoreg_2, ex_mem_1_memwrite_2, halt, halt_ex, halt_mem,
       hazard_unit_1_flushid, hazard_unit_1_flushif, hazard_unit_1_stallid, hazard_unit_1_stallif,
       id_ex_1_alusrc_2, id_ex_1_ble_2, id_ex_1_calc_2, id_ex_1_call_2, id_ex_1_jump_2, id_ex_1_li_2,
       id_ex_1_memread_2, id_ex_1_memtoreg_2, id_ex_1_memwrite_2, id_ex_1_reboot_2, id_ex_1_regdist_2,
       id_ex_1_rtn_2, ishalt, isjump, isjump_ex, isjump_mem, jump, li, mem_wb_1_calc_2, mem_wb_1_li_2,
       mem_wb_1_memtoreg_2, MemRead, MemToReg, MemWrite, or_1_out, reboot, reboot_mem, RegDist, RegWrite,
       RegWrite_ex, RegWrite_mem, RegWrite_wb, rtn, rtn_mem;
  wire [2:0] alu_control_1_out_3, ALUop, Current_Dest_ex, Current_Dest_mem, id_ex_1_aluop_2, id_ex_1_dst1_2,
       id_ex_1_dst2_2, id_ex_1_funct_2, left, right;
  wire [3:0] opcode;
  wire [5:0] if_id_1_out_7;
  wire [15:0] adder_1_out, adder_2_out, alu_1_alu_output, bit_extender_1_out, ex_mem_1_addresult_2,
       ex_mem_1_alu_output, ex_mem_1_immediate_2, ex_mem_1_out1, ex_mem_1_out2, ex_mem_1_pcplus1_2,
       id_ex_1_immediate_2, id_ex_1_jimmediate_2, id_ex_1_out1, id_ex_1_out2, id_ex_1_pcplus1_2,
       if_id_1_out_6, imm, mem_wb_1_aluoutput_2, mem_wb_1_immediate_2, mem_wb_1_readdata_2,
       mem_wb_1_regfiledata_2, multiplexer_1_out, multiplexer_4_out, multiplexer_5_out, multiplexer_6_out,
       multiplexer_7_out, multiplexer_8_out, multiplexer_9_out, PC_q, ra_q, ram_1_data,
       register_file_1_read_data_1, register_file_1_read_data_2, rom_1_data, subtractor_1_out;

  Multiplexer #(.width(16), .enable("false")) multiplexer_1 (
    .in0(multiplexer_6_out), .in1({16{1'b0}}), .out(multiplexer_1_out), .sel(reboot_mem));
  Register #(.width(16)) PC (.D(multiplexer_1_out), .en(hazard_unit_1_stallif), .Q(PC_q), .clk(clk));  // open: clr
  Clock clock_1 (.out(clock_1_out));
  Multiplexer #(.enable("false")) multiplexer_2 (.in0(clock_1_out), .in1(1'b0), .out(clk), .sel(halt));
  ROM #(.addrWidth(16), .dataWidth(16)) rom_1 (.addr(PC_q), .data(rom_1_data));  // open: sel
  Adder #(.width(16)) adder_1 (.a(16'h1), .b(PC_q), .out(adder_1_out));  // open: cin, cout
  Hazard_Unit hazard_unit_1 (
    .clk(clk), .Current_Dest_ex(RegWrite_ex), .RegWrite_ex(Current_Dest_ex), .RegFirst(left),
    .Current_Dest_mem(RegWrite_mem), .RegWrite_mem(Current_Dest_mem), .RegSecond(right), .RegWrite_wb(out_2),
    .Current_Dest_wb(RegWrite_wb), .isjump(isjump), .flushID(hazard_unit_1_flushid),
    .stallIF(hazard_unit_1_stallif), .stallID(hazard_unit_1_stallid), .flushIF(hazard_unit_1_flushif),
    .second(arguments_1_second), .first(arguments_1_first), .ishalt(ishalt), .halt_mem(halt_ex),
    .halt_ex(halt_mem));
  IF_ID if_id_1 (
    .clk(clk), .in_2(adder_1_out), .in_4(rom_1_data), .out_6(if_id_1_out_6), .reset(hazard_unit_1_flushif),
    .out_7({opcode, left, right, if_id_1_out_7}), .Enable(hazard_unit_1_stallid));
  assign bit_extender_1_out = {{4{left[2]}}, {left, right, if_id_1_out_7}};  // Bit_Extender bit_extender_1
  register_file register_file_1 (
    .Write(RegWrite), .Write_Register(out_2), .Write_Data(out_1), .clock(clk), .reset(halt),
    .Read_Regisiter2(right), .Read_Regisiter1(left), .Read_Data_1(register_file_1_read_data_1),
    .Read_Data_2(register_file_1_read_data_2));
  assign imm = {{10{if_id_1_out_7[5]}}, if_id_1_out_7};  // Bit_Extender bit_extender_2
  ID_EX id_ex_1 (
    .MemToReg(MemToReg), .PCplus1(if_id_1_out_6), .RegWrite(RegWrite), .Immediate(imm),
    .ReadData1(register_file_1_read_data_1), .ReadData2(register_file_1_read_data_2),
    .MemToReg_2(id_ex_1_memtoreg_2), .PCPlus1_2(id_ex_1_pcplus1_2), .RegWrite_2(RegWrite_ex),
    .Immediate_2(id_ex_1_immediate_2), .out1(id_ex_1_out1), .out2(id_ex_1_out2), .clk(clk),
    .reset(hazard_unit_1_flushid), .JImmediate(bit_extender_1_out), .JImmediate_2(id_ex_1_jimmediate_2),
    .Funct(if_id_1_out_7[2:0]), .Funct_2(id_ex_1_funct_2), .dst1(if_id_1_out_7[5:3]), .dst2(right),
    .dst1_2(id_ex_1_dst1_2), .dst2_2(id_ex_1_dst2_2), .RegDist(RegDist), .ALUsrc(ALU_src), .ALUop(ALUop),
    .MemRead(MemRead), .RegDist_2(id_ex_1_regdist_2), .ALUsrc_2(id_ex_1_alusrc_2), .ALUop_2(id_ex_1_aluop_2),
    .MemRead_2(id_ex_1_memread_2), .li(li), .li_2(id_ex_1_li_2), .MemWrite(MemWrite),
    .MemWrite_2(id_ex_1_memwrite_2), .ble(ble), .ble_2(id_ex_1_ble_2), .jump(jump), .jump_2(id_ex_1_jump_2),
    .call(call), .call_2(id_ex_1_call_2), .rtn(rtn), .rtn_2(id_ex_1_rtn_2), .reboot(reboot),
    .reboot_2(id_ex_1_reboot_2), .halt(ishalt), .halt_2(halt_ex), .calc(calc), .calc_2(id_ex_1_calc_2));  // open: Destination, Destination_2
  Arguments arguments_1 (.second(arguments_1_second), .First(arguments_1_first), .OPC(opcode));
  Subtractor #(.width(16)) subtractor_1 (.a(id_ex_1_pcplus1_2), .b(16'h1), .out(subtractor_1_out));  // open: bin, bout
  or or_1 (or_1_out, id_ex_1_call_2, id_ex_1_jump_2);
  Multiplexer #(.width(3), .enable("false")) multiplexer_3 (
    .in0(id_ex_1_dst2_2), .in1(id_ex_1_dst1_2), .out(Current_Dest_ex), .sel(id_ex_1_regdist_2));
  ALU alu_1 (
    .input_1(id_ex_1_out1), .input_2(multiplexer_4_out), .ALU_control(alu_control_1_out_3),
    .ALU_output(alu_1_alu_output), .ble(alu_1_ble));
  Multiplexer #(.width(16), .enable("false")) multiplexer_4 (
    .in0(id_ex_1_out2), .in1(id_ex_1_immediate_2), .out(multiplexer_4_out), .sel(id_ex_1_alusrc_2));
  Adder #(.width(16)) adder_2 (.a(subtractor_1_out), .b(multiplexer_5_out), .out(adder_2_out));  // open: cin, cout
  Multiplexer #(.width(16), .enable("false")) multiplexer_5 (
    .in0(id_ex_1_immediate_2), .in1(id_ex_1_jimmediate_2), .out(multiplexer_5_out), .sel(or_1_out));
  or or_2 (isjump_ex, id_ex_1_jump_2, id_ex_1_call_2, id_ex_1_ble_2);
  Multiplexer #(.width(16), .enable("false")) multiplexer_6 (
    .in0(multiplexer_7_out), .in1(ra_q), .out(multiplexer_6_out), .sel(rtn_mem));
  ALU_control alu_control_1 (.ALU_op(id_ex_1_aluop_2), .Funct(id_ex_1_funct_2), .out_3(alu_control_1_out_3));
  and and_1 (and_1_out, call_mem, ~halt_mem);  // AND_Gate
  EX_MEM ex_mem_1 (
    .clk(clk), .reset(1'b0), .MemToReg(id_ex_1_memtoreg_2), .MemToReg_2(ex_mem_1_memtoreg_2),
    .PCplus1(id_ex_1_pcplus1_2), .PCPlus1_2(ex_mem_1_pcplus1_2), .RegWrite(RegWrite_ex),
    .RegWrite_2(RegWrite_mem), .Immediate(id_ex_1_immediate_2), .Immediate_2(ex_mem_1_immediate_2),
    .ReadData1(id_ex_1_out1), .out1(ex_mem_1_out1), .Destination(Current_Dest_ex),
    .Destination_2(Current_Dest_mem), .JImmediate(id_ex_1_jimmediate_2), .ReadData2(id_ex_1_out2),
    .out2(ex_mem_1_out2), .li(id_ex_1_li_2), .li_2(ex_mem_1_li_2), .call(id_ex_1_call_2), .call_2(call_mem),
    .calc(id_ex_1_calc_2), .calc_2(ex_mem_1_calc_2), .MemWrite(id_ex_1_memwrite_2),
    .MemWrite_2(ex_mem_1_memwrite_2), .rtn(id_ex_1_rtn_2), .rtn_2(rtn_mem), .Addresult(adder_2_out),
    .Addresult_2(ex_mem_1_addresult_2), .ble(id_ex_1_ble_2), .ble_2(ex_mem_1_ble_2),
    .reboot(id_ex_1_reboot_2), .reboot_2(reboot_mem), .MemRead(id_ex_1_memread_2),
    .MemRead_2(ex_mem_1_memread_2), .jump(id_ex_1_jump_2), .halt(halt_ex), .halt_2(halt_mem),
    .Jtype(or_1_out), .Jtype_2(ex_mem_1_jtype_2), .ALUble(alu_1_ble), .ALUble_2(ex_mem_1_aluble_2),
    .ALUoutput(alu_1_alu_output), .ALU_output(ex_mem_1_alu_output));  // open: JImmediate_2, jump_2
  Register #(.width(16)) ra (.D(adder_1_out), .en(and_1_out), .Q(ra_q), .clk(clk), .clr(halt_mem));
  Multiplexer #(.width(16), .enable("false")) multiplexer_7 (
    .in0(adder_1_out), .in1(ex_mem_1_addresult_2), .out(multiplexer_7_out), .sel(isjump_mem));
  and and_2 (and_2_out, ex_mem_1_ble_2, ex_mem_1_aluble_2);
  or or_3 (isjump_mem, ex_mem_1_jtype_2, and_2_out);
  RAM #(.addrWidth(16), .dataWidth(16), .bus("separate")) ram_1 (
    .addr(ex_mem_1_alu_output), .din(ex_mem_1_out2), .data(ram_1_data), .str(ex_mem_1_memwrite_2), .clk(clk),
    .ld(ex_mem_1_memread_2));  // open: sel, clr
  MEM_WB mem_wb_1 (
    .MemToReg(ex_mem_1_memtoreg_2), .ALUoutput(ex_mem_1_alu_output), .calc(ex_mem_1_calc_2),
    .Immediate(ex_mem_1_immediate_2), .ReadData(ram_1_data), .Destination(Current_Dest_mem),
    .RegFileData(ex_mem_1_out1), .MemToReg_2(mem_wb_1_memtoreg_2), .ALUoutput_2(mem_wb_1_aluoutput_2),
    .calc_2(mem_wb_1_calc_2), .Immediate_2(mem_wb_1_immediate_2), .ReadData_2(mem_wb_1_readdata_2),
    .Destination_2(out_2), .RegFileData_2(mem_wb_1_regfiledata_2), .clk(clk), .reset(1'b0),
    .li(ex_mem_1_li_2), .li_2(mem_wb_1_li_2), .RegWrite(RegWrite_mem), .RegWrite_2(RegWrite_wb),
    .halt(halt_mem), .halt_2(halt));
  Control Contro_Unitl (
    .A(opcode[3]), .B(opcode[2]), .C(opcode[1]), .D(opcode[0]), .RegDst(RegDist), .RegWrite(RegWrite),
    .ALUsrc(ALU_src), .ALU_OP(ALUop), .MemRead(MemRead), .li(li), .ble(ble), .jump(jump), .call(call),
    .rtn(rtn), .reboot(reboot), .halt(ishalt), .MemWrite(MemWrite), .MemToReg(MemToReg), .calc(calc));
  Multiplexer #(.width(16), .enable("false")) multiplexer_8 (
    .in0(mem_wb_1_readdata_2), .in1(mem_wb_1_aluoutput_2), .out(multiplexer_8_out), .sel(mem_wb_1_memtoreg_2));
  Multiplexer #(.width(16), .enable("false")) multiplexer_9 (
    .in0(multiplexer_8_out), .in1(mem_wb_1_immediate_2), .out(multiplexer_9_out), .sel(mem_wb_1_li_2));
  Multiplexer #(.width(16), .enable("false")) multiplexer_10 (
    .in0(mem_wb_1_regfiledata_2), .in1(multiplexer_9_out), .out(out_1), .sel(mem_wb_1_calc_2));

  // Other names for the same wires on the sheet: Current_Dest_wb[2:0] = out_2

  // Notes on the sheet:
  //   contents of rom_1 (hex, n*v repeats v):
  //   2001 2042 208a 48 a2bf 145e f000
endmodule

// R
module register_file (
  input  Write,
  input  [2:0] Write_Register,
  input  [2:0] Read_Regisiter2,
  input  [2:0] Read_Regisiter1,
  input  [15:0] Write_Data,
  input  clock,
  input  reset,
  output [15:0] Read_Data_1,
  output [15:0] Read_Data_2
);

  wire and_1_out, and_2_out, and_3_out, and_4_out, and_5_out, and_6_out, and_7_out, and_8_out,
       decoder_1_out0, decoder_1_out1, decoder_1_out2, decoder_1_out3, decoder_1_out4, decoder_1_out5,
       decoder_1_out6, decoder_1_out7;
  wire [15:0] register_1_q, register_2_q, register_3_q, register_4_q, register_5_q, register_6_q,
       register_7_q, register_8_q;

  Decoder #(.select(3), .enable("false")) decoder_1 (
    .out0(decoder_1_out0), .out1(decoder_1_out1), .out2(decoder_1_out2), .out3(decoder_1_out3),
    .out4(decoder_1_out4), .out5(decoder_1_out5), .out6(decoder_1_out6), .out7(decoder_1_out7),
    .sel(Write_Register));
  and and_1 (and_1_out, Write, decoder_1_out0);
  and and_2 (and_2_out, Write, decoder_1_out1);
  and and_3 (and_3_out, Write, decoder_1_out2);
  and and_4 (and_4_out, Write, decoder_1_out3);
  and and_5 (and_5_out, Write, decoder_1_out4);
  and and_6 (and_6_out, Write, decoder_1_out5);
  and and_7 (and_7_out, Write, decoder_1_out6);
  and and_8 (and_8_out, Write, decoder_1_out7);
  Register #(.width(16)) register_1 (.D(Write_Data), .en(and_1_out), .Q(register_1_q), .clk(clock), .clr(reset));
  Register #(.width(16)) register_2 (.D(Write_Data), .en(and_2_out), .Q(register_2_q), .clk(clock), .clr(reset));
  Register #(.width(16)) register_3 (.D(Write_Data), .en(and_3_out), .Q(register_3_q), .clk(clock), .clr(reset));
  Register #(.width(16)) register_4 (.D(Write_Data), .en(and_4_out), .Q(register_4_q), .clk(clock), .clr(reset));
  Register #(.width(16)) register_5 (.D(Write_Data), .en(and_5_out), .Q(register_5_q), .clk(clock), .clr(reset));
  Register #(.width(16)) register_6 (.D(Write_Data), .en(and_6_out), .Q(register_6_q), .clk(clock), .clr(reset));
  Register #(.width(16)) register_7 (.D(Write_Data), .en(and_7_out), .Q(register_7_q), .clk(clock), .clr(reset));
  Register #(.width(16)) register_8 (.D(Write_Data), .en(and_8_out), .Q(register_8_q), .clk(clock), .clr(reset));
  Multiplexer #(.select(3), .width(16), .enable("false")) multiplexer_1 (
    .in0(register_1_q), .in1(register_2_q), .in2(register_3_q), .in3(register_4_q), .in4(register_5_q),
    .in5(register_6_q), .in6(register_7_q), .in7(register_8_q), .out(Read_Data_2), .sel(Read_Regisiter2));
  Multiplexer #(.select(3), .width(16), .enable("false")) multiplexer_2 (
    .in0(register_1_q), .in1(register_2_q), .in2(register_3_q), .in3(register_4_q), .in4(register_5_q),
    .in5(register_6_q), .in6(register_7_q), .in7(register_8_q), .out(Read_Data_1), .sel(Read_Regisiter1));
endmodule

module Control (
  input  A,
  input  B,
  input  C,
  input  D,
  output RegWrite,
  output RegDst,
  output ALUsrc,
  output [2:0] ALU_OP,
  output MemRead,
  output li,
  output MemWrite,
  output ble,
  output MemToReg,
  output jump,
  output call,
  output rtn,
  output reboot,
  output halt,
  output calc
);

  wire and_1_out, and_2_out, and_3_out, and_4_out, and_8_out, or_1_out, or_2_out, or_4_out;
  wire [2:0] multiplexer_1_out, multiplexer_2_out, multiplexer_3_out, multiplexer_4_out;

  and R_type (RegDst, ~A, ~B, ~C);  // AND_Gate
  and and_1 (and_1_out, ~A, B, C, D);  // AND_Gate
  and and_2 (and_2_out, A, ~B, ~C, ~D);  // AND_Gate
  and and_3 (and_3_out, A, ~B, ~C, D);  // AND_Gate
  and and_4 (and_4_out, ~A, ~B, C, D);  // AND_Gate
  and and_5 (li, ~A, ~B, C, ~D);  // AND_Gate
  and and_6 (MemRead, ~A, B, ~C, ~D);  // AND_Gate
  and and_7 (MemWrite, ~A, B, ~C, D);  // AND_Gate
  and and_8 (and_8_out, ~A, B, C, ~D);  // AND_Gate
  and and_9 (ble, A, ~B, C, ~D);  // AND_Gate
  and and_10 (jump, A, ~B, C, D);  // AND_Gate
  and and_11 (call, A, B, ~C, ~D);  // AND_Gate
  and and_12 (rtn, A, B, ~C, D);  // AND_Gate
  and and_13 (reboot, A, B, C, ~D);  // AND_Gate
  and and_14 (halt, A, B, C, D);
  or or_1 (or_1_out, and_1_out, or_2_out);
  Multiplexer #(.width(3), .enable("false")) multiplexer_1 (
    .in0(3'b111), .in1(3'b000), .out(multiplexer_1_out), .sel(or_1_out));
  Multiplexer #(.width(3), .enable("false")) multiplexer_2 (
    .in0(3'b111), .in1(3'b001), .out(multiplexer_2_out), .sel(and_2_out));
  Multiplexer #(.width(3), .enable("false")) multiplexer_3 (
    .in0(3'b111), .in1(3'b010), .out(multiplexer_3_out), .sel(and_3_out));
  Multiplexer #(.width(3), .enable("false")) multiplexer_4 (
    .in0(3'b111), .in1(3'b011), .out(multiplexer_4_out), .sel(and_4_out));
  or or_2 (or_2_out, MemRead, MemWrite);
  assign ALU_OP = multiplexer_1_out & multiplexer_2_out & multiplexer_3_out & multiplexer_4_out;  // AND_Gate and_15, 3 bits wide
  or or_3 (ALUsrc, or_1_out, and_2_out, and_3_out, and_4_out);
  or or_4 (or_4_out, and_8_out, ble, jump, call, rtn, reboot, halt);
  not not_1 (calc, or_4_out);
  or or_5 (RegWrite, and_4_out, and_3_out, MemRead, and_8_out, li, RegDst, and_2_out, and_1_out);
  or or_6 (MemToReg, and_3_out, and_2_out, RegDst, and_1_out, and_4_out);
endmodule

module ALU (
  input  [15:0] input_1,
  input  [15:0] input_2,
  input  [2:0] ALU_control,
  output [15:0] ALU_output,
  output ble
);

  wire comparator_1_eq, comparator_1_lt;
  wire [15:0] adder_1_out, and_1_out, bit_extender_1_out, or_1_out, shifter_1_out, shifter_2_out,
       subtractor_1_out;

  Comparator #(.width(16)) comparator_1 (
    .a(input_1), .b(input_2), .eq(comparator_1_eq), .lt(comparator_1_lt));  // open: gt
  Adder #(.width(16)) adder_1 (.a(input_1), .b(input_2), .out(adder_1_out));  // open: cin, cout
  assign or_1_out = input_1 | input_2;  // OR_Gate or_1, 16 bits wide
  assign and_1_out = input_1 & input_2;  // AND_Gate and_1, 16 bits wide
  Subtractor #(.width(16)) subtractor_1 (.a({16{1'b0}}), .b(input_1), .out(subtractor_1_out));  // open: bin, bout
  Shifter #(.width(16)) shifter_1 (.in(input_1), .\dist (input_2[3:0]), .out(shifter_1_out));
  Shifter #(.width(16), .shift("lr")) shifter_2 (.in(input_1), .\dist (input_2[3:0]), .out(shifter_2_out));
  assign bit_extender_1_out = {{15{1'b0}}, comparator_1_lt};  // Bit_Extender bit_extender_1
  or or_2 (ble, comparator_1_lt, comparator_1_eq);
  Multiplexer #(.select(3), .width(16), .enable("false")) multiplexer_1 (
    .in0(adder_1_out), .in1(or_1_out), .in2(and_1_out), .in3(subtractor_1_out), .in4(shifter_1_out),
    .in5(shifter_2_out), .in6(bit_extender_1_out), .out(ALU_output), .sel(ALU_control));  // open: in7
endmodule

module ALU_control (
  input  [2:0] ALU_op,
  input  [2:0] Funct,
  output [2:0] out_3
);

  Multiplexer #(.select(3), .width(3), .enable("false")) multiplexer_1 (
    .in0(ALU_op), .in1(ALU_op), .in2(ALU_op), .in3(ALU_op), .in7(Funct), .out(out_3), .sel(ALU_op));  // open: in4, in5, in6
endmodule

module IF_ID (
  input  clk,
  input  [15:0] in_2,
  input  reset,
  input  [15:0] in_4,
  input  Enable,
  output [15:0] out_6,
  output [15:0] out_7
);

  Register #(.width(16)) register_1 (.D(in_2), .en(Enable), .Q(out_6), .clk(clk), .clr(reset));
  Register #(.width(16)) register_2 (.D(in_4), .en(Enable), .Q(out_7), .clk(clk), .clr(reset));
endmodule

module ID_EX (
  input  clk,
  input  reset,
  input  [2:0] Funct,
  input  MemToReg,
  input  [15:0] PCplus1,
  input  RegWrite,
  input  [15:0] Immediate,
  input  [2:0] dst1,
  input  [15:0] ReadData1,
  input  [2:0] Destination,
  input  [2:0] dst2,
  input  [15:0] JImmediate,
  input  [15:0] ReadData2,
  input  RegDist,
  input  li,
  input  call,
  input  calc,
  input  ALUsrc,
  input  MemWrite,
  input  rtn,
  input  [2:0] ALUop,
  input  ble,
  input  reboot,
  input  MemRead,
  input  jump,
  input  halt,
  output [2:0] Funct_2,
  output MemToReg_2,
  output [15:0] PCPlus1_2,
  output RegWrite_2,
  output [15:0] Immediate_2,
  output [2:0] dst1_2,
  output [15:0] out1,
  output [2:0] Destination_2,
  output [2:0] dst2_2,
  output [15:0] JImmediate_2,
  output [15:0] out2,
  output RegDist_2,
  output li_2,
  output call_2,
  output calc_2,
  output ALUsrc_2,
  output MemWrite_2,
  output rtn_2,
  output [2:0] ALUop_2,
  output ble_2,
  output reboot_2,
  output MemRead_2,
  output jump_2,
  output halt_2
);

  Register #(.width(1)) register_1 (.D(MemToReg), .en(1'b1), .Q(MemToReg_2), .clk(clk), .clr(reset));
  Register #(.width(1)) register_2 (.D(RegWrite), .en(1'b1), .Q(RegWrite_2), .clk(clk), .clr(reset));
  Register #(.width(16)) register_3 (.D(ReadData1), .en(1'b1), .Q(out1), .clk(clk), .clr(reset));
  Register #(.width(16)) register_4 (.D(ReadData2), .en(1'b1), .Q(out2), .clk(clk), .clr(reset));
  Register #(.width(1)) register_5 (.D(RegDist), .en(1'b1), .Q(RegDist_2), .clk(clk), .clr(reset));
  Register #(.width(1)) register_6 (.D(ALUsrc), .en(1'b1), .Q(ALUsrc_2), .clk(clk), .clr(reset));
  Register #(.width(3)) register_7 (.D(ALUop), .en(1'b1), .Q(ALUop_2), .clk(clk), .clr(reset));
  Register #(.width(1)) register_8 (.D(MemRead), .en(1'b1), .Q(MemRead_2), .clk(clk), .clr(reset));
  Register #(.width(1)) register_9 (.D(li), .en(1'b1), .Q(li_2), .clk(clk), .clr(reset));
  Register #(.width(1)) register_10 (.D(MemWrite), .en(1'b1), .Q(MemWrite_2), .clk(clk), .clr(reset));
  Register #(.width(1)) register_11 (.D(ble), .en(1'b1), .Q(ble_2), .clk(clk), .clr(reset));
  Register #(.width(1)) register_12 (.D(jump), .en(1'b1), .Q(jump_2), .clk(clk), .clr(reset));
  Register #(.width(16)) register_13 (.D(PCplus1), .en(1'b1), .Q(PCPlus1_2), .clk(clk), .clr(reset));
  Register #(.width(16)) register_14 (.D(Immediate), .en(1'b1), .Q(Immediate_2), .clk(clk), .clr(reset));
  Register #(.width(3)) register_15 (.D(Destination), .en(1'b1), .Q(Destination_2), .clk(clk), .clr(reset));
  Register #(.width(16)) register_16 (.D(JImmediate), .en(1'b1), .Q(JImmediate_2), .clk(clk), .clr(reset));
  Register #(.width(1)) register_17 (.D(call), .en(1'b1), .Q(call_2), .clk(clk), .clr(reset));
  Register #(.width(1)) register_18 (.D(rtn), .en(1'b1), .Q(rtn_2), .clk(clk), .clr(reset));
  Register #(.width(1)) register_19 (.D(reboot), .en(1'b1), .Q(reboot_2), .clk(clk), .clr(reset));
  Register #(.width(1)) register_20 (.D(halt), .en(1'b1), .Q(halt_2), .clk(clk), .clr(reset));
  Register #(.width(3)) register_21 (.D(Funct), .en(1'b1), .Q(Funct_2), .clk(clk), .clr(reset));
  Register #(.width(3)) register_22 (.D(dst1), .en(1'b1), .Q(dst1_2), .clk(clk), .clr(reset));
  Register #(.width(3)) register_23 (.D(dst2), .en(1'b1), .Q(dst2_2), .clk(clk), .clr(reset));
  Register #(.width(1)) register_24 (.D(calc), .en(1'b1), .Q(calc_2), .clk(clk), .clr(reset));
endmodule

module EX_MEM (
  input  clk,
  input  reset,
  input  MemToReg,
  input  [15:0] PCplus1,
  input  Jtype,
  input  RegWrite,
  input  [15:0] Immediate,
  input  [15:0] ReadData1,
  input  [2:0] Destination,
  input  [15:0] JImmediate,
  input  [15:0] ReadData2,
  input  [15:0] ALUoutput,
  input  li,
  input  call,
  input  calc,
  input  ALUble,
  input  MemWrite,
  input  rtn,
  input  [15:0] Addresult,
  input  ble,
  input  reboot,
  input  MemRead,
  input  jump,
  input  halt,
  output MemToReg_2,
  output [15:0] PCPlus1_2,
  output Jtype_2,
  output RegWrite_2,
  output [15:0] Immediate_2,
  output [15:0] out1,
  output [2:0] Destination_2,
  output [15:0] JImmediate_2,
  output [15:0] out2,
  output [15:0] ALU_output,
  output li_2,
  output call_2,
  output calc_2,
  output ALUble_2,
  output MemWrite_2,
  output rtn_2,
  output [15:0] Addresult_2,
  output ble_2,
  output reboot_2,
  output MemRead_2,
  output jump_2,
  output halt_2
);

  Register #(.width(16)) register_1 (.D(ALUoutput), .en(1'b1), .Q(ALU_output), .clk(clk), .clr(reset));
  Register #(.width(1)) register_2 (.D(ALUble), .en(1'b1), .Q(ALUble_2), .clk(clk), .clr(reset));
  Register #(.width(16)) register_3 (.D(Addresult), .en(1'b1), .Q(Addresult_2), .clk(clk), .clr(reset));
  Register #(.width(1)) register_4 (.D(MemRead), .en(1'b1), .Q(MemRead_2), .clk(clk), .clr(reset));
  Register #(.width(1)) register_5 (.D(MemToReg), .en(1'b1), .Q(MemToReg_2), .clk(clk), .clr(reset));
  Register #(.width(1)) register_6 (.D(RegWrite), .en(1'b1), .Q(RegWrite_2), .clk(clk), .clr(reset));
  Register #(.width(16)) register_7 (.D(ReadData1), .en(1'b1), .Q(out1), .clk(clk), .clr(reset));
  Register #(.width(16)) register_8 (.D(ReadData2), .en(1'b1), .Q(out2), .clk(clk), .clr(reset));
  Register #(.width(1)) register_9 (.D(li), .en(1'b1), .Q(li_2), .clk(clk), .clr(reset));
  Register #(.width(1)) register_10 (.D(MemWrite), .en(1'b1), .Q(MemWrite_2), .clk(clk), .clr(reset));
  Register #(.width(1)) register_11 (.D(ble), .en(1'b1), .Q(ble_2), .clk(clk), .clr(reset));
  Register #(.width(1)) register_12 (.D(jump), .en(1'b1), .Q(jump_2), .clk(clk), .clr(reset));
  Register #(.width(16)) register_13 (.D(PCplus1), .en(1'b1), .Q(PCPlus1_2), .clk(clk), .clr(reset));
  Register #(.width(16)) register_14 (.D(Immediate), .en(1'b1), .Q(Immediate_2), .clk(clk), .clr(reset));
  Register #(.width(3)) register_15 (.D(Destination), .en(1'b1), .Q(Destination_2), .clk(clk), .clr(reset));
  Register #(.width(16)) register_16 (.D(JImmediate), .en(1'b1), .Q(JImmediate_2), .clk(clk), .clr(reset));
  Register #(.width(1)) register_17 (.D(call), .en(1'b1), .Q(call_2), .clk(clk), .clr(reset));
  Register #(.width(1)) register_18 (.D(rtn), .en(1'b1), .Q(rtn_2), .clk(clk), .clr(reset));
  Register #(.width(1)) register_19 (.D(reboot), .en(1'b1), .Q(reboot_2), .clk(clk), .clr(reset));
  Register #(.width(1)) register_20 (.D(halt), .en(1'b1), .Q(halt_2), .clk(clk), .clr(reset));
  Register #(.width(1)) register_21 (.D(Jtype), .en(1'b1), .Q(Jtype_2), .clk(clk), .clr(reset));
  Register #(.width(1)) register_22 (.D(calc), .en(1'b1), .Q(calc_2), .clk(clk), .clr(reset));
endmodule

module MEM_WB (
  input  clk,
  input  reset,
  input  RegWrite,
  input  MemToReg,
  input  [15:0] ALUoutput,
  input  calc,
  input  [15:0] Immediate,
  input  halt,
  input  [15:0] ReadData,
  input  [2:0] Destination,
  input  li,
  input  [15:0] RegFileData,
  output RegWrite_2,
  output MemToReg_2,
  output [15:0] ALUoutput_2,
  output calc_2,
  output [15:0] Immediate_2,
  output halt_2,
  output [15:0] ReadData_2,
  output [2:0] Destination_2,
  output li_2,
  output [15:0] RegFileData_2
);

  Register #(.width(1)) register_1 (.D(MemToReg), .en(1'b1), .Q(MemToReg_2), .clk(clk), .clr(reset));
  Register #(.width(1)) register_2 (.D(calc), .en(1'b1), .Q(calc_2), .clk(clk), .clr(reset));
  Register #(.width(16)) register_3 (.D(ReadData), .en(1'b1), .Q(ReadData_2), .clk(clk), .clr(reset));
  Register #(.width(16)) register_4 (.D(RegFileData), .en(1'b1), .Q(RegFileData_2), .clk(clk), .clr(reset));
  Register #(.width(16)) register_5 (.D(ALUoutput), .en(1'b1), .Q(ALUoutput_2), .clk(clk), .clr(reset));
  Register #(.width(16)) register_6 (.D(Immediate), .en(1'b1), .Q(Immediate_2), .clk(clk), .clr(reset));
  Register #(.width(3)) register_7 (.D(Destination), .en(1'b1), .Q(Destination_2), .clk(clk), .clr(reset));
  Register #(.width(1)) register_8 (.D(li), .en(1'b1), .Q(li_2), .clk(clk), .clr(reset));
  Register #(.width(1)) register_9 (.D(RegWrite), .en(1'b1), .Q(RegWrite_2), .clk(clk), .clr(reset));
  Register #(.width(1)) register_10 (.D(halt), .en(1'b1), .Q(halt_2), .clk(clk), .clr(reset));
endmodule

module Hazard_Unit (
  input  clk,
  input  second,
  input  first,
  input  Current_Dest_ex,
  input  [2:0] RegWrite_ex,
  input  [2:0] RegFirst,
  input  Current_Dest_mem,
  input  [2:0] RegWrite_mem,
  input  [2:0] RegSecond,
  input  [2:0] RegWrite_wb,
  input  Current_Dest_wb,
  input  halt_ex,
  input  ishalt,
  input  halt_mem,
  input  isjump,
  output flushID,
  output stallIF,
  output stallID,
  output flushIF
);

  wire and_1_out, and_2_out, and_3_out, and_4_out, and_5_out, and_6_out, and_7_out, and_8_out, and_9_out,
       and_10_out, and_11_out, comparator_1_eq, comparator_2_eq, comparator_3_eq, comparator_4_eq,
       comparator_5_eq, comparator_6_eq, d_ff_1_q, d_ff_2_q, halt, halt2, not_1_out, or_3_out, or_4_out,
       or_5_out, or_7_out, or_8_out;

  or or_1 (halt, halt_ex, ishalt, halt_mem);
  or or_2 (halt2, halt_mem, halt_ex);
  Comparator #(.width(3)) comparator_1 (.a(RegWrite_ex), .b(RegFirst), .eq(comparator_1_eq));  // open: gt, lt
  Comparator #(.width(3)) comparator_2 (.a(RegWrite_ex), .b(RegSecond), .eq(comparator_2_eq));  // open: gt, lt
  Comparator #(.width(3)) comparator_3 (.a(RegWrite_mem), .b(RegFirst), .eq(comparator_3_eq));  // open: gt, lt
  Comparator #(.width(3)) comparator_4 (.a(RegWrite_mem), .b(RegSecond), .eq(comparator_4_eq));  // open: gt, lt
  Comparator #(.width(3)) comparator_5 (.a(RegWrite_wb), .b(RegFirst), .eq(comparator_5_eq));  // open: gt, lt
  Comparator #(.width(3)) comparator_6 (.a(RegWrite_wb), .b(RegSecond), .eq(comparator_6_eq));  // open: gt, lt
  and and_1 (and_1_out, comparator_1_eq, first);
  and and_2 (and_2_out, comparator_2_eq, second);
  and and_3 (and_3_out, comparator_3_eq, first);
  and and_4 (and_4_out, comparator_4_eq, second);
  and and_5 (and_5_out, comparator_5_eq, first);
  and and_6 (and_6_out, comparator_6_eq, second);
  not not_1 (not_1_out, clk);
  D_Flip_Flop d_ff_1 (.clk(clk), .D(isjump), .Q(d_ff_1_q));  // open: Qn, preset, en, reset
  or or_3 (or_3_out, and_1_out, and_2_out);
  or or_4 (or_4_out, and_3_out, and_4_out);
  or or_5 (or_5_out, and_5_out, and_6_out);
  and and_7 (and_7_out, not_1_out, d_ff_1_q);
  or or_6 (flushIF, and_7_out, halt);
  and and_8 (and_8_out, Current_Dest_ex, or_3_out);
  and and_9 (and_9_out, Current_Dest_mem, or_4_out);
  and and_10 (and_10_out, Current_Dest_wb, or_5_out);
  or or_7 (or_7_out, and_8_out, and_9_out, and_10_out);
  D_Flip_Flop d_ff_2 (.clk(clk), .D(or_7_out), .Q(d_ff_2_q));  // open: Qn, preset, en, reset
  not not_2 (stallIF, or_7_out);
  not not_3 (stallID, or_7_out);
  and and_11 (and_11_out, clk, d_ff_2_q);
  or or_8 (or_8_out, and_11_out, halt2);
  D_Flip_Flop d_ff_3 (.clk(clk), .D(or_8_out), .Q(flushID));  // open: Qn, preset, en, reset
endmodule

module Arguments (
  input  [3:0] OPC,
  output second,
  output First
);

  wire comparator_1_eq, comparator_2_eq, comparator_3_eq, comparator_4_eq, comparator_5_eq, comparator_6_eq,
       comparator_7_eq, comparator_8_eq, comparator_9_eq, comparator_10_eq;

  Comparator #(.width(4)) comparator_1 (.a(4'b0000), .b(OPC), .eq(comparator_1_eq));  // open: gt, lt
  Comparator #(.width(4)) comparator_2 (.a(4'b0001), .b(OPC), .eq(comparator_2_eq));  // open: gt, lt
  Comparator #(.width(4)) comparator_3 (.a(4'b0101), .b(OPC), .eq(comparator_3_eq));  // open: gt, lt
  Comparator #(.width(4)) comparator_4 (.a(4'b1010), .b(OPC), .eq(comparator_4_eq));  // open: gt, lt
  Comparator #(.width(4)) comparator_5 (.a(4'b0011), .b(OPC), .eq(comparator_5_eq));  // open: gt, lt
  Comparator #(.width(4)) comparator_6 (.a(4'b0100), .b(OPC), .eq(comparator_6_eq));  // open: gt, lt
  Comparator #(.width(4)) comparator_7 (.a(4'b0110), .b(OPC), .eq(comparator_7_eq));  // open: gt, lt
  Comparator #(.width(4)) comparator_8 (.a(4'b0111), .b(OPC), .eq(comparator_8_eq));  // open: gt, lt
  Comparator #(.width(4)) comparator_9 (.a(4'b1000), .b(OPC), .eq(comparator_9_eq));  // open: gt, lt
  Comparator #(.width(4)) comparator_10 (.a(4'b1001), .b(OPC), .eq(comparator_10_eq));  // open: gt, lt
  or or_1 (second, comparator_1_eq, comparator_2_eq, comparator_3_eq, comparator_4_eq);
  or or_2 (First, second, comparator_5_eq, comparator_6_eq, comparator_7_eq, comparator_8_eq, comparator_9_eq, comparator_10_eq);
endmodule
